# Fritzing sketch ejercicio_1 (saved by Fritzing 0.9.3b)
breadboards: 1

parts:
  Arduino = Arduino Uno (Rev3) - ICSP
  Button_Yellow = Momentary Switch [package=ksa_sealed_tac_switch]
  Button_Red = Momentary Switch [package=ksa_sealed_tac_switch]
  Button_Green = Momentary Switch [package=ksa_sealed_tac_switch]
  Button_Blue = Momentary Switch [package=ksa_sealed_tac_switch]
  Led_Blue = LED - 5mm [color="Blue (430nm)" package="5 mm [THT]"]
  Led_Green = LED - 5mm [color="Green (560nm)" package="5 mm [THT]"]
  Led_Red = LED - 5mm [color="Red (635nm)" package="5 mm [THT]"]
  Led_Yellow = LED - 5mm [color="Yellow (585nm)" package="5 mm [THT]"]
  R1 = Resistor [tolerance=±5% resistance=220 package=THT]
  R2 = Resistor [tolerance=±5% resistance=220 package=THT]
  R3 = Resistor [tolerance=±5% resistance=220 package=THT]
  R4 = Resistor [tolerance=±5% resistance=220 package=THT]

nets:
  N1: Arduino.GND, Button_Yellow.1, Button_Red.1, Button_Green.1, Button_Blue.1, Led_Blue.cathode, Led_Green.cathode, Led_Red.cathode, Led_Yellow.cathode
  N2: Arduino.D2, R1.Pin_1
  N3: Arduino.D3_PWM, R2.Pin_1
  N4: Arduino.D4, R3.Pin_1
  N5: Arduino.D5_PWM, R4.Pin_1
  N6: Led_Blue.anode, R1.Pin_0
  N7: Led_Green.anode, R2.Pin_0
  N8: Led_Red.anode, R3.Pin_0
  N9: Led_Yellow.anode, R4.Pin_0
