# Fritzing sketch ejercicio_2 (saved by Fritzing 0.9.3b)
breadboards: 1

parts:
  Arduino = Arduino Uno (Rev3) - ICSP
  Button_Yellow = Momentary Switch [package=ksa_sealed_tac_switch]
  Button_Red = Momentary Switch [package=ksa_sealed_tac_switch]
  Button_Green = Momentary Switch [package=ksa_sealed_tac_switch]
  Button_Blue = Momentary Switch [package=ksa_sealed_tac_switch]
  Led_Blue = LED - 5mm [color="Blue (430nm)" package="5 mm [THT]"]
  Led_Green = LED - 5mm [color="Green (560nm)" package="5 mm [THT]"]
  Led_Red = LED - 5mm [color="Red (635nm)" package="5 mm [THT]"]
  Led_Yellow = LED - 5mm [color="Yellow (585nm)" package="5 mm [THT]"]
  R1 = Resistor [tolerance=±5% resistance=220 package=THT]
  R2 = Resistor [tolerance=±5% resistance=220 package=THT]
  R3 = Resistor [tolerance=±5% resistance=220 package=THT]
  R4 = Resistor [tolerance=±5% resistance=220 package=THT]
  R5 = Resistor [tolerance=±5% resistance=10k package=THT]
  R7 = Resistor [tolerance=±5% resistance=10k package=THT]
  R9 = Resistor [tolerance=±5% resistance=10k package=THT]
  R11 = Resistor [tolerance=±5% resistance=10k package=THT]

nets:
  N1: Arduino.A0, Button_Blue.3, R5.Pin_1
  N2: Arduino.A1, Button_Green.3, R7.Pin_1
  N3: Arduino.A2, Button_Red.3, R9.Pin_1
  N4: Arduino.A3, Button_Yellow.3, R11.Pin_1
  N5: Arduino.GND, Button_Yellow.1, Button_Red.1, Button_Green.1, Button_Blue.1, Led_Blue.cathode, Led_Green.cathode, Led_Red.cathode, Led_Yellow.cathode
  N6: Arduino.D2, R1.Pin_1
  N7: Arduino.D3_PWM, R2.Pin_1
  N8: Arduino.D4, R3.Pin_1
  N9: Arduino.D5_PWM, R4.Pin_1
  N10: Arduino.5V, R5.Pin_0, R7.Pin_0, R9.Pin_0, R11.Pin_0
  N11: Led_Blue.anode, R1.Pin_0
  N12: Led_Green.anode, R2.Pin_0
  N13: Led_Red.anode, R3.Pin_0
  N14: Led_Yellow.anode, R4.Pin_0
